# Fritzing sketch driveboard (saved by Fritzing 0.8.3b)
circuit board: 19.05cm x 17.78cm

parts:
  laser = RJ45
  XTAL1 = Crystal [frequency="16 Mhz" package=THT]
  x2 = RJ45
  x1 = RJ45
  y2 = RJ45
  z1 = RJ45
  z2 = RJ45
  door2 = RJ45
  door1 = RJ45
  chiller = RJ45
  stepper_y = RJ45
  stepper_x = RJ45
  stepper_z = RJ45
  Atmega328P = atmega168 [package=dip]
  R1 = Resistor [tolerance=±5% resistance=10k package=THT]
  R2 = Resistor [tolerance=±5% resistance=10k package=THT]
  R3 = Resistor [tolerance=±5% resistance=10k package=THT]
  R9 = Resistor [tolerance=±5% resistance=10k package=THT]
  R8 = Resistor [tolerance=±5% resistance=10k package=THT]
  R7 = Resistor [tolerance=±5% resistance=10k package=THT]
  R5 = Resistor [tolerance=±5% resistance=10k package=THT]
  R6 = Resistor [tolerance=±5% resistance=10k package=THT]
  R4 = Resistor [tolerance=±5% resistance=10k package=THT]
  C2 = Ceramic Capacitor [capacitance=22pF package="100 mil [THT, multilayer]"]
  C1 = Ceramic Capacitor [capacitance=22pF package="100 mil [THT, multilayer]"]
  ICSP = double row female pin header, 6 pins [form="♀ (female)"]
  Gecko_(G203V/G201X)_Z-axis = female pin header, 12 pins [form="♀ (female)"]
  Gecko_(G203V/G201X)_Y-axis = female pin header, 12 pins [form="♀ (female)"]
  Gecko_(G203V/G201X)_X-axis = female pin header, 12 pins [form="♀ (female)"]
  IN2 = screw terminal, 6 pins
  IN1 = screw terminal, 6 pins
  24V = screw terminal, 6 pins
  IN3 = screw terminal, 6 pins
  air_relay = IC, DIP package, 4 pins [chip_label=SSR part_number=AQY212GHA]
  aux1_relay = IC, DIP package, 4 pins [chip_label=SSR part_number=AQY212GHA]
  SSR_AC3 = female pin header, 1 pin [form="♀ (female)"]
  SSR_AC4 = female pin header, 1 pin [form="♀ (female)"]
  SSR_DC+ = female pin header, 1 pin [form="♀ (female)"]
  SSR_DC- = female pin header, 1 pin [form="♀ (female)"]
  D1 = Rectifier Diode [part_number=1N4004 package="300 mil [THT]"]
  D2 = Rectifier Diode [part_number=1N4004 package="300 mil [THT]"]
  R10 = Resistor [tolerance=±5% resistance=360 package=THT]
  R11 = Resistor [tolerance=±5% resistance=360 package=THT]
  P9 = double row female pin header, 44 pins [form="♀ (female)"]
  P8 = double row female pin header, 44 pins [form="♀ (female)"]
  R12 = Resistor [tolerance=±5% resistance=6.5k package=THT]
  R13 = Resistor [tolerance=±5% resistance=10k package=THT]
  R14 = Resistor [tolerance=±5% resistance=6.5k package=THT]
  R15 = Resistor [tolerance=±5% resistance=20k package=THT]
  R16 = Resistor [tolerance=±5% resistance=20k package=THT]
  stepperterm1 = screw terminal, 6 pins
  stepperterm2 = screw terminal, 6 pins
  power5V = female pin header, 2 pins [form="♀ (female)"]
  y1 = RJ45
  NAND = IC, DIP package, 14 pins [chip_label=NAND]
  AND = IC, DIP package, 14 pins [chip_label=AND]
  G2 = female pin header, 1 pin [form="♀ (female)"]
  G1 = female pin header, 1 pin [form="♀ (female)"]
  G4 = female pin header, 1 pin [form="♀ (female)"]
  G3 = female pin header, 1 pin [form="♀ (female)"]
  G6 = female pin header, 1 pin [form="♀ (female)"]
  G5 = female pin header, 1 pin [form="♀ (female)"]
  G8 = female pin header, 1 pin [form="♀ (female)"]
  G7 = female pin header, 1 pin [form="♀ (female)"]
  G10 = female pin header, 1 pin [form="♀ (female)"]
  G9 = female pin header, 1 pin [form="♀ (female)"]
  G12 = female pin header, 1 pin [form="♀ (female)"]
  G11 = female pin header, 1 pin [form="♀ (female)"]
  G13 = female pin header, 1 pin [form="♀ (female)"]
  G14 = female pin header, 1 pin [form="♀ (female)"]
  G15 = female pin header, 1 pin [form="♀ (female)"]
  G16 = female pin header, 1 pin [form="♀ (female)"]
  G17 = female pin header, 1 pin [form="♀ (female)"]
  G18 = female pin header, 1 pin [form="♀ (female)"]
  G19 = female pin header, 1 pin [form="♀ (female)"]
  G20 = female pin header, 1 pin [form="♀ (female)"]
  G21 = female pin header, 1 pin [form="♀ (female)"]
  G22 = female pin header, 1 pin [form="♀ (female)"]
  G23 = female pin header, 1 pin [form="♀ (female)"]
  G24 = female pin header, 1 pin [form="♀ (female)"]
  G25 = female pin header, 1 pin [form="♀ (female)"]
  G26 = female pin header, 1 pin [form="♀ (female)"]
  auto_reset = female pin header, 2 pins [form="♀ (female)"]
  D5 = female pin header, 2 pins [form="♀ (female)"]
  J1 = female pin header, 6 pins [form="♀ (female)"]
  J2 = female pin header, 4 pins [form="♀ (female)"]
  J3 = female pin header, 6 pins [form="♀ (female)"]
  J4 = female pin header, 4 pins [form="♀ (female)"]
  J5 = female pin header, 6 pins [form="♀ (female)"]
  J6 = female pin header, 4 pins [form="♀ (female)"]
  RaspberryPi_(optional) = double row female pin header, 26 pins [form="♀ (female)"]
  gecko_sense = Resistor [tolerance=±5% resistance=3k package=THT]
  SMC11_sense_(optional) = Resistor [tolerance=±5% resistance=3k package=THT]
  interlocks = RJ45
  G27 = female pin header, 1 pin [form="♀ (female)"]
  G28 = female pin header, 1 pin [form="♀ (female)"]
  keylock = female pin header, 2 pins [form="♀ (female)"]
  e-stop = female pin header, 2 pins [form="♀ (female)"]
  assists = RJ45
  G29 = female pin header, 1 pin [form="♀ (female)"]  # not connected
  G30 = female pin header, 1 pin [form="♀ (female)"]  # not connected
  serial = female pin header, 4 pins [form="♀ (female)"]
  C3 = Electrolytic Capacitor [capacitance=1mF voltage=50V package="300 mil [THT, electrolytic]"]
  C4 = Ceramic Capacitor [capacitance=100nF voltage=50V package="100 mil [THT, multilayer]"]
  C5 = Ceramic Capacitor [capacitance=100nF voltage=50V package="100 mil [THT, multilayer]"]
  C6 = Ceramic Capacitor [capacitance=100nF voltage=50V package="100 mil [THT, multilayer]"]
  C7 = Ceramic Capacitor [capacitance=100nF voltage=50V package="100 mil [THT, multilayer]"]
  C9 = Ceramic Capacitor [capacitance=100nF package="100 mil [THT, multilayer]"]
  C10 = Ceramic Capacitor [capacitance=100nF package="100 mil [THT, multilayer]"]
  C11 = Ceramic Capacitor [capacitance=100nF voltage=50V package="100 mil [THT, multilayer]"]
  C12 = Electrolytic Capacitor [capacitance=47µF voltage=50V package="100 mil [THT, electrolytic]"]
  extension = double row female pin header, 6 pins [form="♀ (female)"]

nets:
  N1: laser.pin_1, laser.pin_3, x2.pin_1, x2.pin_3, x1.pin_1, x1.pin_3, y2.pin_1, y2.pin_3, z1.pin_1, z1.pin_3, z2.pin_1, z2.pin_3, door2.pin_1, door2.pin_3, door1.pin_1, door1.pin_3, chiller.pin_1, chiller.pin_3, Atmega328P.VCC, Atmega328P.AVCC, ICSP.pin6, IN3.pin2, SSR_DC+.pin1, P9.pin2, P9.pin43, power5V.pin2, y1.pin_1, y1.pin_3, NAND.pin1, NAND.pin9, NAND.pin13, NAND.pin14, AND.pin9, AND.pin14, RaspberryPi_(optional).pin1, serial.pin1, C3.-, C4.1, C6.0, C7.1, C9.0, C10.0, C11.0, C12.-, extension.pin1
  N2: laser.pin_2, laser.pin_6, NAND.pin8
  N3: laser.pin_4, Atmega328P.D6_(PWM)
  N4: laser.pin_5, Atmega328P.D5_(PWM), D5.pin1
  N5: laser.pin_7, laser.pin_8, x2.pin_7, x2.pin_8, x1.pin_7, x1.pin_8, y2.pin_7, y2.pin_8, z1.pin_7, z1.pin_8, z2.pin_7, z2.pin_8, door2.pin_7, door2.pin_8, door1.pin_7, door1.pin_8, chiller.pin_7, chiller.pin_8, Atmega328P.GND, R1.Pin_1, R2.Pin_1, R3.Pin_1, R9.Pin_1, R8.Pin_1, R7.Pin_1, R5.Pin_1, R6.Pin_1, R4.Pin_1, C2.1, C1.1, ICSP.pin4, Gecko_(G203V/G201X)_Z-axis.pin3, Gecko_(G203V/G201X)_Y-axis.pin3, Gecko_(G203V/G201X)_X-axis.pin3, air_relay.pin2, aux1_relay.pin2, SSR_DC-.pin1, P9.pin21, P9.pin22, P9.pin23, P9.pin24, R13.Pin_0, power5V.pin1, y1.pin_7, y1.pin_8, NAND.pin7, AND.pin7, G2.pin1, G1.pin1, G4.pin1, G3.pin1, G6.pin1, G5.pin1, G8.pin1, G7.pin1, G10.pin1, G9.pin1, G12.pin1, G11.pin1, G13.pin1, G14.pin1, G15.pin1, G16.pin1, G17.pin1, G18.pin1, G19.pin1, G20.pin1, G21.pin1, G22.pin1, G23.pin1, G24.pin1, G25.pin1, G26.pin1, D5.pin2, RaspberryPi_(optional).pin3, gecko_sense.Pin_0, interlocks.pin_1, interlocks.pin_3, e-stop.pin1, serial.pin2, C3.+, C6.1, C7.0, C9.1, C10.1, C11.1, C12.+, extension.pin2
  N6: XTAL1.pin_0, Atmega328P.XLAT1, C2.0
  N7: XTAL1.pin_1, Atmega328P.XLAT2, C1.0
  N8: x2.pin_2, x2.pin_4, x2.pin_5, x2.pin_6, Atmega328P.A1, R2.Pin_0, AND.pin4
  N9: x1.pin_2, x1.pin_4, x1.pin_5, x1.pin_6, Atmega328P.A0, R1.Pin_0, AND.pin5
  N10: y2.pin_2, y2.pin_4, y2.pin_5, y2.pin_6, Atmega328P.A3, R4.Pin_0, AND.pin2
  N11: z1.pin_2, z1.pin_4, z1.pin_5, z1.pin_6, Atmega328P.A4, R5.Pin_0, AND.pin1
  N12: z2.pin_2, z2.pin_4, z2.pin_5, z2.pin_6, Atmega328P.A5, R6.Pin_0, AND.pin13
  N13: door2.pin_2, door2.pin_4, door2.pin_5, door2.pin_6, R8.Pin_0, AND.pin11
  N14: door1.pin_2, door1.pin_4, door1.pin_5, door1.pin_6, R9.Pin_0, AND.pin10
  N15: chiller.pin_2, chiller.pin_4, chiller.pin_5, chiller.pin_6, Atmega328P.D3_(PWM), R7.Pin_0, NAND.pin10
  N16: stepper_y.pin_1, stepper_y.pin_3, Gecko_(G203V/G201X)_Y-axis.pin10, stepperterm1.pin2, J4.pin1
  N17: stepper_y.pin_2, stepper_y.pin_6, Gecko_(G203V/G201X)_Y-axis.pin9, stepperterm1.pin1, J4.pin2
  N18: stepper_y.pin_4, stepper_y.pin_8, Gecko_(G203V/G201X)_Y-axis.pin8, stepperterm2.pin6, J4.pin3
  N19: stepper_y.pin_5, stepper_y.pin_7, Gecko_(G203V/G201X)_Y-axis.pin7, stepperterm2.pin5, J4.pin4
  N20: stepper_x.pin_1, stepper_x.pin_3, Gecko_(G203V/G201X)_X-axis.pin10, stepperterm1.pin6, J2.pin1
  N21: stepper_x.pin_2, stepper_x.pin_6, Gecko_(G203V/G201X)_X-axis.pin9, stepperterm1.pin5, J2.pin2
  N22: stepper_x.pin_4, stepper_x.pin_8, Gecko_(G203V/G201X)_X-axis.pin8, stepperterm1.pin4, J2.pin3
  N23: stepper_x.pin_5, stepper_x.pin_7, Gecko_(G203V/G201X)_X-axis.pin7, stepperterm1.pin3, J2.pin4
  N24: stepper_z.pin_1, stepper_z.pin_3, Gecko_(G203V/G201X)_Z-axis.pin10, stepperterm2.pin4, J6.pin1
  N25: stepper_z.pin_2, stepper_z.pin_6, Gecko_(G203V/G201X)_Z-axis.pin9, stepperterm2.pin3, J6.pin2
  N26: stepper_z.pin_4, stepper_z.pin_8, Gecko_(G203V/G201X)_Z-axis.pin8, stepperterm2.pin2, J6.pin3
  N27: stepper_z.pin_5, stepper_z.pin_7, Gecko_(G203V/G201X)_Z-axis.pin7, stepperterm2.pin1, J6.pin4
  N28: Atmega328P.RESET, ICSP.pin3, P8.pin21, auto_reset.pin1, auto_reset.pin2, RaspberryPi_(optional).pin25
  N29: Atmega328P.D0_(RX), P9.pin11, RaspberryPi_(optional).pin4, serial.pin4
  N30: Atmega328P.D1_(TX), R12.Pin_1
  N31: Atmega328P.D2, NAND.pin5, AND.pin8
  N32: Atmega328P.D4, R10.Pin_0
  N33: Atmega328P.D7, R11.Pin_1
  N34: Atmega328P.D8, Gecko_(G203V/G201X)_X-axis.pin4, J1.pin4
  N35: Atmega328P.D9_(PWM), Gecko_(G203V/G201X)_Y-axis.pin4, J3.pin4
  N36: Atmega328P.D10_(PWM), Gecko_(G203V/G201X)_Z-axis.pin4, J5.pin4
  N37: Atmega328P.D11_(PWM), ICSP.pin5, Gecko_(G203V/G201X)_X-axis.pin5, J1.pin3
  N38: Atmega328P.D12, ICSP.pin1, Gecko_(G203V/G201X)_Y-axis.pin5, J3.pin3
  N39: Atmega328P.D13, ICSP.pin2, Gecko_(G203V/G201X)_Z-axis.pin5, J5.pin3
  N40: Atmega328P.A2, R3.Pin_0, y1.pin_2, y1.pin_4, y1.pin_5, y1.pin_6, AND.pin3
  N41: Gecko_(G203V/G201X)_Z-axis.pin1, R16.Pin_1
  N42: Gecko_(G203V/G201X)_Z-axis.pin2, R16.Pin_0
  N43: Gecko_(G203V/G201X)_Z-axis.pin11, Gecko_(G203V/G201X)_Y-axis.pin11, Gecko_(G203V/G201X)_X-axis.pin11, 24V.pin6, air_relay.pin3, aux1_relay.pin3, J1.pin1, J3.pin1, J5.pin1, C5.1
  N44: Gecko_(G203V/G201X)_Z-axis.pin12, Gecko_(G203V/G201X)_Y-axis.pin12, Gecko_(G203V/G201X)_X-axis.pin12, 24V.pin1, 24V.pin3, 24V.pin5, D1.anode, D2.anode, J1.pin2, J1.pin5, J1.pin6, J3.pin2, J3.pin5, J3.pin6, J5.pin2, J5.pin5, J5.pin6, assists.pin_2, assists.pin_4, assists.pin_6, assists.pin_8, C5.0
  N45: Gecko_(G203V/G201X)_Y-axis.pin1, R15.Pin_1
  N46: Gecko_(G203V/G201X)_Y-axis.pin2, R15.Pin_0
  N47: Gecko_(G203V/G201X)_X-axis.pin1, R14.Pin_1
  N48: Gecko_(G203V/G201X)_X-axis.pin2, R14.Pin_0
  N49: IN2.pin1, IN2.pin2, IN3.pin3, IN3.pin4, IN3.pin5, IN3.pin6
  N50: IN2.pin3, IN2.pin4, SSR_AC3.pin1
  N51: IN2.pin5, IN2.pin6, IN1.pin1, SSR_AC4.pin1
  N52: IN1.pin2, IN1.pin3, IN1.pin4, IN1.pin5, IN1.pin6
  N53: 24V.pin2, aux1_relay.pin4, D2.cathode, assists.pin_5, assists.pin_7
  N54: 24V.pin4, air_relay.pin4, D1.cathode, assists.pin_1, assists.pin_3
  N55: IN3.pin1, interlocks.pin_5, interlocks.pin_7, G27.pin1, G28.pin1, keylock.pin2, C4.0
  N56: air_relay.pin1, R10.Pin_1
  N57: aux1_relay.pin1, R11.Pin_0
  N58: P9.pin1, RaspberryPi_(optional).pin26, SMC11_sense_(optional).Pin_1, extension.pin6
  N59: P9.pin12, R12.Pin_0, R13.Pin_1, RaspberryPi_(optional).pin5, serial.pin3
  N60: P8.pin23, RaspberryPi_(optional).pin24, extension.pin3
  N61: P8.pin24, RaspberryPi_(optional).pin23, extension.pin4
  N62: P8.pin25, RaspberryPi_(optional).pin21, extension.pin5
  N63: P8.pin26, RaspberryPi_(optional).pin13, gecko_sense.Pin_1, SMC11_sense_(optional).Pin_0
  N64: NAND.pin2, NAND.pin6
  N65: NAND.pin3, AND.pin12
  N66: NAND.pin4, AND.pin6
  N67: NAND.pin11, NAND.pin12
  N68: interlocks.pin_2, interlocks.pin_4, interlocks.pin_6, interlocks.pin_8, keylock.pin1, e-stop.pin2

notes:
  Lasersaur
  AC_in_2
  AC_laser_psu_1
  AC_in_1
  AC_5V_psu_1
  AC_extra_1
  AC_extra_2
  (12A max)
  AC_24V_psu_1
  AC_laser_psu_2
  AC_5V_psu_2
  AC_24V_psu_2
  GND_in
  DC_in_5V-
  aux1_assist+
  GND_laser_psu
  (AC total ->12A max)
  (5A max)
  GND_24V_psu
  DC_in_5V+
  GND_5V_psu
  aux1_assist-
  GND_extra
  air_assist-
  air_assist+
  GND_frame
  DriveBoard  v13.06
  DC_in_24V-
  DC_in_24V+
  3
  4
  46
  45
  TX
  RX (UART1)
  5V (VDD)
  gnd
  PB1
  PB5
  PB0
  PD7
  PD5
  PD4
  PD2
  RX
  PC5
  PC0
  VCC
  IN1
  OUT1
  OUT3
  IN3
  IN2
  OUT2
  GND
  voltage_divider
  A
  A'
  B
  B'
  grn<->wgrn
  BeagleBone
  24V
  dis
  dir
  step
  current_set
  11.5k
  360
  first four pins do not connect
  10k
  6.49k
  (optional)
  (screw terminals -> 5A max)
  1
  pwm:blu, dis:grn, gnd:brn
  cable mapping -> A:wgr/wor, A':gr/or, B:bl/wbl, B':br/wbr
  *
  1000uF
  22pF
  -----------
  aux2:wbl
  align pins here at this side
  Nanotec SMC11 (optional) X-axis
  Nanotec SMC11 (optional) Y-axis
  Nanotec SMC11 (optional) Z-axis
  (modular jacks -> 3A max)
  (1A max)
  MC74AC11NG
  MC74AC10NG
  GPIO_2
  GPIO_3
  GPIO_4
  GPIO_17
  GPIO2_12
  GPIO2_7
  GPIO2_22
  GPIO_7
  Nanotec:   6.49K
  R = 47*I/(7–I)*1000
  5V
  GPIO2_6
  GPIO2_8
  GPIO2_10
  3.3V
  LinE: 11.5K
  (both interlocks need
  to be closed for operation)
  100nF
  47uF
  BeagleBone Black (P8)
  BeagleBone Black (P9)
  X
  Y
  Z
  DriveBoard v13.06
